// Logisim project Logisim模型机设计.circ as structural Verilog: 9 circuits, main circuit main
module main (
  input  RST
);

  wire CLK, clock_1_out, controlled_buffer_1_out, enHAR, enIR, enMAR, enMDR, enPC, EX, FE, GateAdr, GateALU,
       GateCLK, GateJNZ, GateMDR, GatePC, GateWData, LoadDRAM, LoadPC, LoadRj, LoadS, not_1_out, not_2_out,
       R0, R1, R2, R3, R4, R5, R6, R7, SELECT, SIGN, T0, T1, T2;
  wire [2:0] OP, RD, RS;
  wire [3:0] H_Adr_q, HAdr;
  wire [7:0] ACC, controlled_buffer_2_out, demultiplexer_1_out0, demultiplexer_1_out1, demultiplexer_1_out2,
       demultiplexer_1_out3, demultiplexer_1_out4, demultiplexer_1_out5, demultiplexer_1_out6,
       demultiplexer_1_out7, MAR_q, MDR_q, PC, pcjnz_1_out_3, R1_q, R2_q, R3_q, R4_q, R5_q, R6_q, R7_q,
       ram_1_data, WData, \运算器_1_out ;
  wire [7:4] IR;

  assign controlled_buffer_1_out = LoadS ? CLK : 1'bz;  // Controlled_Buffer controlled_buffer_1
  result result_1 (.in_1(controlled_buffer_2_out), .out_4(SIGN), .CLK(controlled_buffer_1_out), .CLR(RST));
  \运算器  \u_运算器_1  (.S2(OP[2]), .S1(OP[1]), .S0(OP[0]), .RI(WData), .ACC(ACC), .OUT(\运算器_1_out ), .SELECT(SELECT));
  Register #(.width(4), .trigger("falling")) H_Adr (.D(HAdr), .en(enHAR), .Q(H_Adr_q), .clk(CLK), .clr(RST));
  Counter #(.trigger("falling")) u_PC (
    .load(LoadPC), .D(controlled_buffer_2_out), .count(enPC), .Q(PC), .clk(CLK), .clr(RST));  // open: carry
  assign controlled_buffer_2_out = GateJNZ ? pcjnz_1_out_3 : 8'bz;  // Controlled_Buffer controlled_buffer_2
  PCJNZ pcjnz_1 (.Ir({IR, HAdr}), .PC(PC), .out_3(pcjnz_1_out_3));
  // Probe on \运算器_1_out 
  assign controlled_buffer_2_out = GatePC ? PC : 8'bz;  // Controlled_Buffer controlled_buffer_3
  assign controlled_buffer_2_out = GateALU ? \运算器_1_out  : 8'bz;  // Controlled_Buffer controlled_buffer_4
  assign controlled_buffer_2_out = GateAdr ? {H_Adr_q, HAdr} : 8'bz;  // Controlled_Buffer controlled_buffer_5
  Register #(.trigger("falling")) MAR (.D(controlled_buffer_2_out), .en(enMAR), .Q(MAR_q), .clk(CLK), .clr(RST));
  Demultiplexer #(.select(3), .width(8), .enable("false")) demultiplexer_1 (
    .out0(demultiplexer_1_out0), .out1(demultiplexer_1_out1), .out2(demultiplexer_1_out2),
    .out3(demultiplexer_1_out3), .out4(demultiplexer_1_out4), .out5(demultiplexer_1_out5),
    .out6(demultiplexer_1_out6), .out7(demultiplexer_1_out7), .in(controlled_buffer_2_out), .sel(RD));
  // Probe on RD
  RAM ram_1 (.addr(MAR_q), .data(ram_1_data), .clk(CLK), .ld(LoadDRAM));  // open: sel, clr
  assign ram_1_data = not_1_out ? controlled_buffer_2_out : 8'bz;  // Controlled_Buffer controlled_buffer_6
  not not_1 (not_1_out, LoadDRAM);
  Register #(.trigger("falling")) R0_ACC (.D(demultiplexer_1_out0), .en(R0), .Q(ACC), .clk(CLK), .clr(RST));
  Register #(.trigger("falling")) u_R1 (.D(demultiplexer_1_out1), .en(R1), .Q(R1_q), .clk(CLK), .clr(RST));
  Register #(.trigger("falling")) u_R2 (.D(demultiplexer_1_out2), .en(R2), .Q(R2_q), .clk(CLK), .clr(RST));
  Register #(.trigger("falling")) u_R3 (.D(demultiplexer_1_out3), .en(R3), .Q(R3_q), .clk(CLK), .clr(RST));
  Register #(.trigger("falling")) u_R4 (.D(demultiplexer_1_out4), .en(R4), .Q(R4_q), .clk(CLK), .clr(RST));
  Register #(.trigger("falling")) u_R5 (.D(demultiplexer_1_out5), .en(R5), .Q(R5_q), .clk(CLK), .clr(RST));
  Register #(.trigger("falling")) u_R6 (.D(demultiplexer_1_out6), .en(R6), .Q(R6_q), .clk(CLK), .clr(RST));
  Register #(.trigger("falling")) u_R7 (.D(demultiplexer_1_out7), .en(R7), .Q(R7_q), .clk(CLK), .clr(RST));
  Register #(.trigger("falling")) MDR (.D(ram_1_data), .en(enMDR), .Q(MDR_q), .clk(CLK), .clr(RST));
  // Probe on ACC
  Multiplexer #(.select(3), .width(8), .enable("false")) multiplexer_1 (
    .in0(ACC), .in1(R1_q), .in2(R2_q), .in3(R3_q), .in4(R4_q), .in5(R5_q), .in6(R6_q), .in7(R7_q),
    .out(WData), .sel(RS));
  // Probe on RS
  assign controlled_buffer_2_out = GateMDR ? MDR_q : 8'bz;  // Controlled_Buffer controlled_buffer_7
  assign controlled_buffer_2_out = GateWData ? WData : 8'bz;  // Controlled_Buffer controlled_buffer_8
  // Probe on WData
  Register #(.trigger("falling")) u_IR (.D(controlled_buffer_2_out), .en(enIR), .Q({IR, HAdr}), .clk(CLK), .clr(RST));
  assign CLK = not_2_out ? clock_1_out : 1'bz;  // Controlled_Buffer controlled_buffer_9
  not not_2 (not_2_out, GateCLK);
  Clock clock_1 (.out(clock_1_out));
  time3 time3_1 (.Clock(CLK), .RSet(RST), .T0(T0), .T1(T1), .T2(T2));
  CU cu_1 (
    .IR({IR, HAdr}), .T0(T0), .T1(T1), .T2(T2), .FE(FE), .EX(EX), .GatePC(GatePC), .enMAR(enMAR),
    .enMDR(enMDR), .enPC(enPC), .GateMDR(GateMDR), .enIR(enIR), .LoadRj(LoadRj), .GateALU(GateALU),
    .SELECT(SELECT), .OP(OP), .RS(RS), .RD(RD), .enHAR(enHAR), .GateAdr(GateAdr), .LoadDRAM(LoadDRAM),
    .LoadPC(LoadPC), .GateJNZ(GateJNZ), .GateCLK(GateCLK), .GateWData(GateWData), .LoadS(LoadS), .SIGN(SIGN));
  time2 time2_1 (.Clock(T0), .RSet(RST), .T0(FE), .T1(EX));
  Decoder #(.select(3), .disabled(0)) decoder_1 (
    .out0(R0), .out1(R1), .out2(R2), .out3(R3), .out4(R4), .out5(R5), .out6(R6), .out7(R7), .sel(RD),
    .en(LoadRj));
  // Probe on RD

  // Other names for the same wires on the sheet: CLR = RST; IR[3:0] = HAdr
endmodule

module time3 (
  input  Clock,
  input  RSet,
  output T0,
  output T1,
  output T2
);

  D_Flip_Flop d_ff_1 (.clk(Clock), .D(T2), .Q(T0), .preset(RSet));  // open: Qn, en, reset
  D_Flip_Flop d_ff_2 (.clk(Clock), .D(T0), .Q(T1), .reset(RSet));  // open: Qn, preset, en
  D_Flip_Flop d_ff_3 (.clk(Clock), .D(T1), .Q(T2), .reset(RSet));  // open: Qn, preset, en
endmodule

module time2 (
  input  Clock,
  input  RSet,
  output T0,
  output T1
);

  D_Flip_Flop d_ff_1 (.clk(Clock), .D(T1), .Q(T0), .preset(RSet));  // open: Qn, en, reset
  D_Flip_Flop d_ff_2 (.clk(Clock), .D(T0), .Q(T1), .reset(RSet));  // open: Qn, preset, en
endmodule

module \运算器  (
  input  S2,
  input  S1,
  input  S0,
  input  SELECT,
  input  [7:0] RI,
  input  [7:0] ACC,
  output [7:0] OUT
);

  wire [7:0] ADD, AND, DEC, INC, multiplexer_1_out, multiplexer_2_out, NOT, SHL, SHR;

  SHL shl_1 (.OUT(SHL), .IN(RI));
  SHR shr_1 (.OUT(SHR), .IN(RI));
  Adder adder_1 (.a(RI), .b(ACC), .out(ADD));  // open: cin, cout
  assign AND = RI & ACC;  // AND_Gate and_1, 8 bits wide
  assign NOT = ~RI;  // NOT_Gate not_1, 8 bits wide
  Adder adder_2 (.a(RI), .b(8'h1), .out(INC));  // open: cin, cout
  Subtractor subtractor_1 (.a(RI), .b(8'h1), .out(DEC));  // open: bin, bout
  Multiplexer #(.select(3), .width(8), .disabled(0), .enable("false")) multiplexer_1 (
    .in0(ADD), .in1(AND), .in2(NOT), .in3(ACC), .in4(SHL), .in5(SHR), .in6(INC), .in7(DEC),
    .out(multiplexer_1_out), .sel({S2, S1, S0}));
  Multiplexer #(.select(3), .width(8), .disabled(0), .enable("false")) multiplexer_2 (
    .in1(RI), .in2(ACC), .in3(ACC), .out(multiplexer_2_out), .sel({S2, S1, S0}));  // open: in0, in4, in5, in6, in7
  Multiplexer #(.width(8), .disabled(0), .enable("false")) multiplexer_3 (
    .in0(multiplexer_1_out), .in1(multiplexer_2_out), .out(OUT), .sel(SELECT));

  // Other names for the same wires on the sheet: MOV[7:0] = ACC; R[7:0] = RI
endmodule

module SHL (
  input  [7:0] IN,
  output [7:0] OUT
);


  assign OUT = {IN[6:0], 1'b0};
endmodule

module SHR (
  input  [7:0] IN,
  output [7:0] OUT
);


  assign OUT = {1'b0, IN[7:1]};
endmodule

module CU (
  input  [7:0] IR,
  input  T0,
  input  T1,
  input  T2,
  input  FE,
  input  EX,
  input  SIGN,
  output GatePC,
  output enMAR,
  output enMDR,
  output enPC,
  output GateMDR,
  output enIR,
  output LoadRj,
  output GateALU,
  output SELECT,
  output [2:0] OP,
  output [2:0] RS,
  output enHAR,
  output GateAdr,
  output LoadDRAM,
  output LoadPC,
  output GateJNZ,
  output GateCLK,
  output GateWData,
  output LoadS,
  output [2:0] RD
);

  wire and_1_out, and_5_out, and_6_out, and_8_out, and_10_out, and_11_out, and_12_out, and_14_out,
       and_15_out, and_17_out, and_18_out, and_19_out, and_20_out, and_21_out, and_22_out, and_23_out,
       and_25_out, and_26_out, and_27_out, JMP, JNZ, LAH, LD, LDA, nand_1_out, nand_2_out, not_1_out,
       not_2_out, not_3_out, or_1_out, or_3_out, or_4_out, or_8_out, or_9_out, or_12_out, ST, STA;

  Decoder #(.select(3), .disabled(0)) decoder_1 (
    .out0(LDA), .out1(LD), .out2(STA), .out3(ST), .out4(LAH), .out5(JMP), .out6(JNZ), .out7(GateCLK),
    .sel(IR[6:4]), .en(IR[7]));
  Multiplexer #(.width(3), .disabled(0), .enable("false")) multiplexer_1 (
    .in0(3'b000), .in1(IR[2:0]), .out(RD), .sel(or_1_out));
  or or_1 (or_1_out, IR[6], IR[5]);
  // Probe on IR[6:4]
  and and_1 (and_1_out, EX, ST, T1);
  and and_2 (GatePC, T0, FE);
  and and_3 (enHAR, EX, LAH, T2);
  and and_4 (LoadDRAM, nand_1_out, nand_2_out);
  nand nand_1 (nand_1_out, EX, STA, T2);
  or or_2 (enMAR, and_1_out, and_6_out, and_5_out);
  and and_5 (and_5_out, EX, or_3_out, T0);
  and and_6 (and_6_out, T0, FE);
  or or_3 (or_3_out, LDA, STA, LD);
  and and_7 (enPC, T1, FE);
  nand nand_2 (nand_2_out, EX, ST, T2);
  and and_8 (and_8_out, T2, FE);
  and and_9 (enIR, T2, FE);
  and and_10 (and_10_out, EX, or_4_out, T0);
  or or_4 (or_4_out, LDA, STA);
  or or_5 (GateMDR, and_8_out, and_17_out);
  and and_11 (and_11_out, EX, not_1_out, T2);
  not not_1 (not_1_out, IR[7]);
  or or_6 (GateAdr, and_10_out, and_12_out);
  and and_12 (and_12_out, EX, JMP, T2);
  and and_13 (GateWData, EX, ST, T1);
  or or_7 (LoadRj, and_11_out, and_14_out);
  and and_14 (and_14_out, EX, or_8_out, T2);
  or or_8 (or_8_out, LDA, LD);
  and and_15 (and_15_out, EX, JMP, T2);
  and and_16 (LoadS, EX, not_2_out, T2);
  not not_2 (not_2_out, IR[7]);
  and and_17 (and_17_out, EX, or_9_out, T2);
  or or_9 (or_9_out, LDA, LD);
  and and_18 (and_18_out, EX, not_3_out, T2);
  not not_3 (not_3_out, IR[7]);
  or or_10 (LoadPC, and_15_out, and_19_out);
  and and_19 (and_19_out, EX, and_20_out, T2);
  and and_20 (and_20_out, JNZ, SIGN);
  and and_21 (and_21_out, T1, FE);
  or or_11 (enMDR, and_21_out, and_22_out);
  and and_22 (and_22_out, EX, or_12_out, T1);
  or or_12 (or_12_out, LDA, LD);
  or or_13 (GateALU, and_18_out, and_23_out, and_26_out, and_27_out);
  and and_23 (and_23_out, EX, LD, T0);
  and and_24 (GateJNZ, EX, and_25_out, T2);
  and and_25 (and_25_out, JNZ, SIGN);
  and and_26 (and_26_out, EX, STA, T2);
  and and_27 (and_27_out, EX, ST, T2);

  assign OP = IR[6:4];
  assign RS = IR[2:0];
  assign SELECT = IR[7];

  // Other names for the same wires on the sheet: Ri[2:0] = IR[2:0]; PC_plus_plus = enPC; STP = GateCLK
endmodule

module PCJNZ (
  input  [7:0] Ir,
  input  [7:0] PC,
  output [7:0] out_3
);

  // Probe on {{5{Ir[3]}}, Ir[2:0]}
  Adder adder_1 (.a({{5{Ir[3]}}, Ir[2:0]}), .b(PC), .out(out_3));  // open: cin, cout

  // Other names for the same wires on the sheet: 扩展码[7:0] = {{5{Ir[3]}}, Ir[2:0]}
endmodule

module result (
  input  [7:0] in_1,
  input  CLK,
  input  CLR,
  output out_4
);

  wire or_1_out;

  or or_1 (or_1_out, in_1[0], in_1[1], in_1[2], in_1[3], in_1[4], in_1[5], in_1[6], in_1[7]);
  Register #(.width(1), .trigger("falling")) register_1 (.D(or_1_out), .Q(out_4), .clk(CLK), .clr(CLR));  // open: en
endmodule
