// Logisim project logisim 入门.circ as structural Verilog: 32 circuits, main circuit 按钮
module \按钮  (
);

  wire button_1_out;

  Button button_1 (.out(button_1_out));
  LED led_1 (.in(button_1_out));
endmodule

module \从零开始  (
  input  [3:0] y,
  input  [3:0] x,
  input  [7:0] in_3,
  output [3:0] test,
  output [3:0] out_5
);

  wire [3:0] undriven, undriven_2, xor_2_out;

  // Probe on y
  // Probe on x
  // Probe on x
  // Probe on in_3
  assign test = y ^ x;  // XOR_Gate xor_1, 4 bits wide
  assign xor_2_out = ~undriven ^ undriven_2;  // XOR_Gate xor_2, 4 bits wide
  // Probe on in_3
  // Probe on test
  // Probe on y
  // Probe on in_3
  assign out_5 = test & y;  // AND_Gate and_1, 4 bits wide
  // Probe on in_3

  // Other names for the same wires on the sheet: TY[3:0] = y
endmodule

module \不同颜色线缆  (
  input  \引脚类型不对 ,
  input  [1:0] in_2,
  input  in_3
);

  wire undriven;
  wire [1:0] nand_2_out, undriven_3;
  wire [1:1] undriven_2;

  nand nand_1 (\引脚类型不对 , 1'b1, 1'b0, undriven, 1'b1);
  assign nand_2_out = ~(in_2 & undriven_3 & {undriven_2[1], in_3});  // NAND_Gate nand_2, 2 bits wide
  // Pins of 1 and 2 bits meet at {undriven_2[1], in_3}

  // Notes on the sheet:
  //   深绿色表示高电平
  //   蓝色表示未知状态
  //   灰色表示飞线
  //   亮绿色表示高电平
  //   红色表示信号冲突
  //   黑色表示多位总线
  //   橙色表示位宽不匹配
  //   华中科技大学计算机学院 计算机组成原理
endmodule

module \探针  (
  input  [7:0] in_1
);

  // Probe on in_1
  // Probe on in_1
  // Probe on in_1
  // Probe on in_1
endmodule

module \分线器使用  (
  input  [7:0] in_1
);


  // Notes on the sheet:
  //   华中科技大学计算机学院 计算机组成原理
  //   8分二，高位在下
  //   只分部分位，位宽不对称
  //   8分8
  //   分线器不分输入输出，可反向使用进行线缆汇总
  //   8分二，高位在上
  //   8分3，3+3+2
  //   只分1位，如取符号位
endmodule

module \摇杆  (
  output [3:0] out_1,
  output [3:0] out_2
);

  Joystick joystick_1 (.x(out_1), .y(out_2));
endmodule

module \键盘  (
  input  \读使能 ,
  input  \清除缓冲区 ,
  input  \写使能 ,
  input  \清除屏幕 ,
  output \缓冲区有字符 
);

  wire \时钟信号_out ;
  wire [6:0] keyboard_1_data;

  Clock \u_时钟信号  (.out(\时钟信号_out ));
  Keyboard keyboard_1 (.clk(\时钟信号_out ), .re(\读使能 ), .clr(\清除缓冲区 ), .avail(\缓冲区有字符 ), .data(keyboard_1_data));
  TTY #(.rows(4), .cols(24)) tty_1 (.data(keyboard_1_data), .clk(\时钟信号_out ), .we(\写使能 ), .clr(\清除屏幕 ));

  // Notes on the sheet:
  //   键盘
  //   文字终端
endmodule

module \LED点阵  (
  input  [6:0] x,
  input  [6:0] x_2,
  input  [6:0] x_3,
  input  [6:0] x_4,
  input  [6:0] x_5
);

  DotMatrix dotmatrix_1 (.col0(x), .col1(x_5), .col2(x_2), .col3(x_3), .col4(x_4));
endmodule

module \数码管  (
  input  [3:0] in_1,
  input  in_2,
  input  [3:0] in_3,
  input  [3:0] in_4
);

  _7_Segment_Display u_7_segment_display_1 (
    .g(in_1[3]), .f(in_1[2]), .a(in_1[1]), .b(in_1[0]), .e(in_4[3]), .d(in_4[2]), .c(in_4[1]), .dp(in_4[0]));
  Hex_Digit_Display hex_digit_display_1 (.value(in_3), .dp(in_2));
endmodule

module \三态门  (
  input  \输入 ,
  input  in_2,
  input  in_3,
  input  in_4,
  input  \控制端 ,
  input  in_6,
  input  in_7,
  input  in_8,
  input  \输入_2 ,
  input  in_10,
  input  in_11,
  input  in_12,
  input  \控制端_2 ,
  input  in_14,
  input  in_15,
  input  in_16,
  output \输出 ,
  output out_18,
  output out_19,
  output out_20,
  output \输出_2 ,
  output out_22,
  output out_23,
  output out_24
);

  assign \输出  = \控制端  ? \输入  : 1'bz;  // Controlled_Buffer controlled_buffer_1
  assign \输出_2  = \控制端_2  ? ~\输入_2  : 1'bz;  // Controlled_Inverter controlled_inverter_1
  assign out_18 = in_6 ? in_2 : 1'bz;  // Controlled_Buffer controlled_buffer_2
  assign out_22 = in_14 ? ~in_10 : 1'bz;  // Controlled_Inverter controlled_inverter_2
  assign out_19 = in_7 ? in_3 : 1'bz;  // Controlled_Buffer controlled_buffer_3
  assign out_23 = in_15 ? ~in_11 : 1'bz;  // Controlled_Inverter controlled_inverter_3
  assign out_20 = in_8 ? in_4 : 1'bz;  // Controlled_Buffer controlled_buffer_4
  assign out_24 = in_16 ? ~in_12 : 1'bz;  // Controlled_Inverter controlled_inverter_4
endmodule

module \复用器  (
  input  [3:0] \第0路输入 ,
  input  [3:0] in_2,
  input  [3:0] \第1路输入 ,
  input  [3:0] in_4,
  input  [3:0] \第2路输入 ,
  input  [3:0] in_6,
  input  [1:0] \选择端 ,
  input  \使能端 ,
  input  [1:0] \选择端_2 ,
  input  \使能端_2 ,
  input  [3:0] \第3路输入 ,
  input  [3:0] in_12,
  output [3:0] \输出 ,
  output [3:0] \输出_2 
);

  Multiplexer #(.select(2), .width(4)) multiplexer_1 (
    .in0(\第0路输入 ), .in1(\第1路输入 ), .in2(\第2路输入 ), .in3(\第3路输入 ), .out(\输出 ), .sel(\选择端 ), .en(\使能端 ));
  Multiplexer #(.select(2), .width(4)) multiplexer_2 (
    .in0(in_2), .in1(in_4), .in2(in_6), .in3(in_12), .out(\输出_2 ), .sel(\选择端_2 ), .en(\使能端_2 ));
endmodule

module \解复用器  (
  input  [3:0] \输入 ,
  input  [3:0] \输入_2 ,
  input  \使能端 ,
  input  [1:0] \选择端 ,
  input  \使能端_2 ,
  input  [1:0] \选择端_2 ,
  output [3:0] \第0路输出 ,
  output [3:0] out_8,
  output [3:0] \第1路输出 ,
  output [3:0] out_10,
  output [3:0] \第2路输出 ,
  output [3:0] out_12,
  output [3:0] \第3路输出 ,
  output [3:0] out_14
);

  Demultiplexer #(.select(2), .width(4)) demultiplexer_1 (
    .out0(\第0路输出 ), .out1(\第1路输出 ), .out2(\第2路输出 ), .out3(\第3路输出 ), .in(\输入 ), .sel(\选择端 ), .en(\使能端 ));
  Demultiplexer #(.select(2), .width(4), .tristate("true")) demultiplexer_2 (
    .out0(out_8), .out1(out_10), .out2(out_12), .out3(out_14), .in(\输入_2 ), .sel(\选择端_2 ), .en(\使能端_2 ));
endmodule

module \译码器  (
  input  \使能端 ,
  input  [1:0] \选择端 ,
  input  \使能端_2 ,
  input  [1:0] \选择端_2 ,
  output \第0路 ,
  output out_6,
  output \第1路 ,
  output out_8,
  output \第2路 ,
  output out_10,
  output \第3路 ,
  output out_12
);

  Decoder #(.select(2), .tristate("true")) decoder_1 (
    .out0(\第0路 ), .out1(\第1路 ), .out2(\第2路 ), .out3(\第3路 ), .sel(\选择端 ), .en(\使能端 ));
  Decoder #(.select(2)) decoder_2 (
    .out0(out_6), .out1(out_8), .out2(out_10), .out3(out_12), .sel(\选择端_2 ), .en(\使能端_2 ));
endmodule

module \优先编码器  (
  input  in_1,
  input  in_2,
  input  in_3,
  input  in_4,
  input  in_5,
  input  in_6,
  input  in_7,
  input  in_8,
  input  \请求0 ,
  input  in_10,
  input  in_11,
  input  \请求2 ,
  input  in_13,
  input  in_14,
  input  \请求4 ,
  input  in_16,
  input  in_17,
  input  \请求6 ,
  input  in_19,
  input  in_20,
  input  \使能输入端 ,
  input  \使能输入端_2 ,
  input  \使能输入端_3 ,
  output [2:0] out_24,
  output out_25,
  output \使能输出 ,
  output \使能输出_2 ,
  output \使能输出_3 ,
  output [2:0] \编号 ,
  output [2:0] \编号_2 ,
  output [2:0] \编号_3 ,
  output \有请求 ,
  output \有请求_2 ,
  output \有请求_3 
);

  wire undriven, undriven_2, undriven_3, undriven_4, undriven_5, undriven_6, undriven_7, undriven_8,
       undriven_9, undriven_10, undriven_11, undriven_12;

  Priority_Encoder priority_encoder_1 (
    .in0(\请求0 ), .in1(undriven), .in2(\请求2 ), .in3(undriven_2), .in4(\请求4 ), .in5(undriven_3), .in6(\请求6 ),
    .in7(undriven_4), .out(\编号 ), .en_in(\使能输入端 ), .gs(\有请求 ), .en_out(\使能输出 ));
  Priority_Encoder priority_encoder_2 (
    .in0(in_1), .in1(in_2), .in2(in_3), .in3(in_4), .in4(in_5), .in5(in_6), .in6(in_7), .in7(in_8),
    .out(out_24), .gs(out_25));  // open: en_in, en_out
  Priority_Encoder priority_encoder_3 (
    .in0(in_10), .in1(undriven_5), .in2(in_13), .in3(undriven_6), .in4(in_16), .in5(undriven_7), .in6(in_19),
    .in7(undriven_8), .out(\编号_2 ), .en_in(\使能输入端_2 ), .gs(\有请求_2 ), .en_out(\使能输出_2 ));
  Priority_Encoder priority_encoder_4 (
    .in0(in_11), .in1(undriven_9), .in2(in_14), .in3(undriven_10), .in4(in_17), .in5(undriven_11),
    .in6(in_20), .in7(undriven_12), .out(\编号_3 ), .en_in(\使能输入端_3 ), .gs(\有请求_3 ), .en_out(\使能输出_3 ));

  // Notes on the sheet:
  //   请求1
  //   请求3
  //   请求5
  //   请求7
endmodule

module \位选择器  (
  input  [7:0] in_1,
  input  [2:0] in_2,
  output out_3
);

  BitSelector bitselector_1 (.in(in_1), .out(out_3), .sel(in_2));
endmodule

module \D触发器  (
  input  in_1,
  input  \异步清零 ,
  input  \异步置位 ,
  input  \使能端 ,
  output out_5,
  output Q_prime
);

  wire clock_1_out, s_r_ff_1_q;

  Clock clock_1 (.out(clock_1_out));
  D_Flip_Flop d_ff_1 (.preset(\异步置位 ), .en(\使能端 ), .reset(\异步清零 ));  // open: clk, D, Q, Qn
  D_Flip_Flop d_ff_2 (.clk(clock_1_out), .D(in_1), .Q(out_5));  // open: Qn, preset, en, reset
  T_Flip_Flop t_ff_1 (.preset(\异步置位 ), .reset(\异步清零 ), .en(\使能端 ));  // open: clk, T, Q, Qn
  S_R_Flip_Flop s_r_ff_1 (
    .Q(s_r_ff_1_q), .Qn(Q_prime), .preset(\异步置位 ), .reset(\异步清零 ), .en(\使能端 ));  // open: S, clk, R
  J_K_Flip_Flop j_k_ff_1 (.preset(\异步置位 ), .en(\使能端 ), .reset(\异步清零 ));  // open: J, clk, K, Q, Qn
endmodule

module \寄存器  (
  input  [3:0] \输入 ,
  input  \使能端 ,
  input  \异步清零 ,
  output [3:0] \输出 
);

  wire \时钟_out ;

  Register #(.width(4)) register_1 (.D(\输入 ), .en(\使能端 ), .Q(\输出 ), .clk(\时钟_out ), .clr(\异步清零 ));
  Clock \u_时钟  (.out(\时钟_out ));
endmodule

module \计数器  (
  input  Load,
  input  [7:0] \初值 ,
  input  Count,
  input  \异步清零 ,
  output [7:0] \计数器输出 ,
  output Carry
);

  wire \时钟_out ;

  Clock \u_时钟  (.out(\时钟_out ));
  Counter counter_1 (.load(Load), .D(\初值 ), .count(Count), .Q(\计数器输出 ), .carry(Carry), .clk(\时钟_out ), .clr(\异步清零 ));
endmodule

module \移位寄存器  (
  input  load,
  input  shift,
  input  [3:0] \input ,
  input  \异步清零 ,
  output [3:0] \最后段输出 
);

  wire \时钟_out ;
  wire [3:0] shift_register_1_q0, shift_register_1_q1, shift_register_1_q2, shift_register_1_q3,
       shift_register_1_q4, shift_register_1_q5, undriven, undriven_2, undriven_3, undriven_4, undriven_5,
       undriven_6;

  Clock \u_时钟  (.out(\时钟_out ));
  Shift_Register #(.width(4), .length(6)) shift_register_1 (
    .shift(shift), .in(\input ), .clk(\时钟_out ), .out(\最后段输出 ), .load(load), .clr(\异步清零 ), .d0(undriven),
    .q0(shift_register_1_q0), .d1(undriven_2), .q1(shift_register_1_q1), .d2(undriven_3),
    .q2(shift_register_1_q2), .d3(undriven_4), .q3(shift_register_1_q3), .d4(undriven_5),
    .q4(shift_register_1_q4), .d5(undriven_6), .q5(shift_register_1_q5));
  // Probe on shift_register_1_q1
  // Probe on shift_register_1_q0
  // Probe on shift_register_1_q3
  // Probe on shift_register_1_q5
  // Probe on shift_register_1_q2
  // Probe on shift_register_1_q4
  // Probe on \最后段输出 

  // Notes on the sheet:
  //   并发载入端口
  //   移位寄存器并发输出
endmodule

module \随机数产生器  (
  input  \使能端 ,
  input  \使能端_2 ,
  input  \异步复位 ,
  input  \异步复位_2 ,
  output [7:0] \随机数 ,
  output [7:0] \随机数_2 
);

  wire \时钟_out ;

  Clock \u_时钟  (.out(\时钟_out ));
  Random random_1 (.clk(\时钟_out ), .next(\使能端 ), .out(\随机数 ), .clr(\异步复位 ));
  Random random_2 (.clk(\时钟_out ), .next(\使能端_2 ), .out(\随机数_2 ), .clr(\异步复位_2 ));
endmodule

module \毛刺现象  (
  input  in_1,
  output out_2
);

  wire and_2_out, and_3_out, buffer_1_out, clock_1_out, not_1_out, not_2_out, not_3_out;

  Clock clock_1 (.out(clock_1_out));
  not not_1 (not_1_out, in_1);
  Counter counter_1 (.clk(clock_1_out));  // open: load, D, count, Q, carry, clr
  Counter counter_2 (.clk(clock_1_out));  // open: load, D, count, Q, carry, clr
  // Probe on in_1
  // Probe on not_1_out
  not not_2 (not_2_out, clock_1_out);
  not not_3 (not_3_out, clock_1_out);
  buf buffer_1 (buffer_1_out, clock_1_out);
  and and_1 (out_2, in_1, not_1_out);
  and and_2 (and_2_out, not_2_out, clock_1_out);
  and and_3 (and_3_out, not_3_out, buffer_1_out);
  Counter counter_3 (.clk(and_2_out));  // open: load, D, count, Q, carry, clr
  Counter counter_4 (.clk(and_3_out));  // open: load, D, count, Q, carry, clr

  // Notes on the sheet:
  //   增加缓冲器，使得延迟一样，避免毛刺
  //   此计数器不可能计数，但试试看？为什么？
  //   修改后正常
  //   用计数器观察调试毛刺
endmodule

module \存储器  (
  input  [7:0] \地址 ,
  input  [7:0] \写数据 ,
  input  RAM_Write,
  input  RAM_Read,
  output [7:0] \读数据 
);

  wire clock_1_out;

  RAM ram_1 ();  // open: addr, data, sel, clk, ld, clr
  Clock clock_1 (.out(clock_1_out));
  RAM #(.bus("asynch")) ram_2 ();  // open: addr, data, sel, ld, clr
  RAM #(.bus("separate")) ram_3 (
    .addr(\地址 ), .din(\写数据 ), .data(\读数据 ), .str(RAM_Write), .clk(clock_1_out), .ld(RAM_Read));  // open: sel, clr
  RAM #(.bus("separate")) ram_4 ();  // open: addr, din, data, str, sel, clk, ld, clr

  // Notes on the sheet:
  //   双向输入输出引脚同步模式
  //   时钟
  //   双向输入输出异步模式
  //   输入输出分离同步模式
  //   单向输出
endmodule

module ROM (
  input  [7:0] \地址 ,
  input  \片选信号 ,
  output [7:0] \_8位数据输出 ,
  output [15:0] \_16位数据输出 ,
  output [31:0] \_32位数据输出 
);

  ROM_part rom_1 (.addr(\地址 ), .data(\_8位数据输出 ), .sel(\片选信号 ));
  ROM_part #(.dataWidth(16)) rom_2 (.addr(\地址 ), .data(\_16位数据输出 ), .sel(\片选信号 ));
  ROM_part #(.dataWidth(32)) rom_3 (.addr(\地址 ), .data(\_32位数据输出 ), .sel(\片选信号 ));

  // Notes on the sheet:
  //   contents of rom_1 (hex, n*v repeats v):
  //   66 4*0 12
  //   contents of rom_2 (hex, n*v repeats v):
  //   6666 0 8888 0 0 1234 82*0 456
  //   contents of rom_3 (hex, n*v repeats v):
  //   4*0 6666666 12345678 bceddd66 a
endmodule

module \震荡电路  (
  input  in_1,
  output out_2
);

  nand nand_1 (out_2, in_1, out_2);

  // Notes on the sheet:
  //   尝试修改输入引脚的电平,输入输出存在反馈，导致电路状态不稳定
  //   如出现类似情况，尝试去掉部分回路连接直至故障消除
  //   华中科技大学计算机学院 计算机组成原理
endmodule

module \信号冲突  (
  input  in_1,
  input  in_2,
  output out_3
);


  assign in_2 = in_1;
  assign out_3 = in_1;

  // Notes on the sheet:
  //   输入相同时无问题，不同时出错，红色显示
  //   华中科技大学计算机学院 计算机组成原理
endmodule

module \异常反馈  (
  input  in_1,
  input  in_2,
  output out_3
);

  wire not_1_out;

  Multiplexer #(.enable("false")) multiplexer_1 (.in0(in_1), .in1(in_2), .out(out_3), .sel(not_1_out));
  not not_1 (not_1_out, out_3);

  // Notes on the sheet:
  //   类似震荡
endmodule

module bitadder (
  input  [7:0] data1,
  input  [7:0] data2,
  output [4:0] \输入数据中比特位为1的数目 
);

  BitAdder bitadder_1 (.in0(data1), .in1(data2), .out(\输入数据中比特位为1的数目 ));
endmodule

module adder (
  input  \进位输入 ,
  input  [3:0] \加数1 ,
  input  [3:0] \加数2 ,
  output [3:0] \和数 ,
  output \进位输出 
);

  // Probe on \加数1 
  // Probe on \加数2 
  // Probe on \和数 
  Adder #(.width(4)) adder_1 (.a(\加数1 ), .b(\加数2 ), .out(\和数 ), .cin(\进位输入 ), .cout(\进位输出 ));
endmodule

module shift (
  input  [7:0] \数据输入 ,
  input  [7:0] \数据输入_2 ,
  input  [2:0] \移位位数 ,
  input  [2:0] \移位位数_2 ,
  input  [7:0] \数据输入_3 ,
  input  [7:0] \数据输入_4 ,
  input  [2:0] \移位位数_3 ,
  input  [2:0] \移位位数_4 ,
  output [7:0] \数据输出 ,
  output [7:0] \数据输出_2 ,
  output [7:0] \数据输出_3 ,
  output [7:0] \数据输出_4 
);

  Shifter #(.shift("lr")) shifter_1 (.in(\数据输入 ), .\dist (\移位位数 ), .out(\数据输出 ));
  Shifter #(.shift("rl")) shifter_2 (.in(\数据输入_3 ), .\dist (\移位位数_3 ), .out(\数据输出_3 ));
  Shifter #(.shift("ar")) shifter_3 (.in(\数据输入_2 ), .\dist (\移位位数_2 ), .out(\数据输出_2 ));
  Shifter #(.shift("rr")) shifter_4 (.in(\数据输入_4 ), .\dist (\移位位数_4 ), .out(\数据输出_4 ));

  // Notes on the sheet:
  //   逻辑右移
  //   循环左移
  //   算术右移
  //   循环右移
endmodule

module \乘法  (
  input  [3:0] \进位输入 ,
  input  [3:0] \被乘数 ,
  input  [3:0] \乘数 ,
  output [3:0] \乘积低位 ,
  output [3:0] \进位输出_乘积高位 
);

  // Probe on \被乘数 
  // Probe on \乘数 
  Multiplier #(.width(4)) multiplier_1 (.a(\被乘数 ), .b(\乘数 ), .out(\乘积低位 ), .cin(\进位输入 ), .cout(\进位输出_乘积高位 ));
  // Probe on \乘积低位 
  // Probe on {\进位输出_乘积高位 , \乘积低位 }
endmodule

module \除法  (
  input  [3:0] \被除数高4位 ,
  input  [3:0] \被除数低4位 ,
  input  [3:0] \除数 ,
  output [3:0] \商 ,
  output [3:0] \余数 
);

  // Probe on {\被除数高4位 , \被除数低4位 }
  // Probe on \除数 
  Divider #(.width(4)) divider_1 (.a(\被除数低4位 ), .b(\除数 ), .out(\商 ), .upper(\被除数高4位 ), .rem(\余数 ));
  // Probe on \商 
endmodule

module \求补器  (
  input  [7:0] \输入数据 ,
  output [7:0] \补码 
);

  // Probe on \输入数据 
  // Probe on \补码 
  Negator negator_1 (.in(\输入数据 ), .out(\补码 ));
endmodule
